// Logisim project MEMORY.circ as structural Verilog: 10 circuits, main circuit Main
module RSTrigger (
  input  S,
  input  C,
  input  R,
  output Q,
  output nQ
);

  wire nand_1_out, nand_2_out;

  nand nand_1 (nand_1_out, S, C);
  nand nand_2 (nand_2_out, C, R);
  nand nand_3 (Q, nand_1_out, nQ);
  nand nand_4 (nQ, Q, nand_2_out);
endmodule

module JKTrigger (
  input  J,
  input  C,
  input  K,
  output Q,
  output nQ
);

  wire and_1_out, and_2_out, not_1_out, s_r_ff_1_q, s_r_ff_1_qn;

  and and_1 (and_1_out, nQ, J);
  and and_2 (and_2_out, K, Q);
  not not_1 (not_1_out, C);
  S_R_Flip_Flop s_r_ff_1 (
    .S(and_1_out), .clk(C), .R(and_2_out), .Q(s_r_ff_1_q), .Qn(s_r_ff_1_qn));  // open: preset, reset, en
  S_R_Flip_Flop s_r_ff_2 (.S(s_r_ff_1_q), .clk(not_1_out), .R(s_r_ff_1_qn), .Q(Q), .Qn(nQ));  // open: preset, reset, en
endmodule

// C
module DDTriger (
  input  D,
  input  C,
  output Q
);

  wire not_1_out;

  not not_1 (not_1_out, D);
  JKTrigger jktrigger_1 (.J(D), .C(C), .K(not_1_out), .Q(Q));  // open: nQ
endmodule

module _2bit (
  input  D1,
  input  D2,
  input  C,
  output Q1,
  output Q2
);

  DDTriger ddtriger_1 (.C(C), .Q(Q1), .D(D1));
  DDTriger ddtriger_2 (.C(C), .Q(Q2), .D(D2));
endmodule

module _4bit (
  input  D1,
  input  D2,
  input  D3,
  input  D4,
  input  C,
  output Q1,
  output Q2,
  output Q3,
  output Q4
);

  _2bit u_2bit_1 (.D1(D1), .D2(D2), .C(C), .Q1(Q1), .Q2(Q2));
  _2bit u_2bit_2 (.D1(D3), .D2(D4), .C(C), .Q1(Q3), .Q2(Q4));
endmodule

module _8bit (
  input  D1,
  input  D2,
  input  D3,
  input  D4,
  input  D5,
  input  D6,
  input  D7,
  input  D8,
  input  C,
  output Q1,
  output Q2,
  output Q3,
  output Q4,
  output Q5,
  output Q6,
  output Q7,
  output Q8
);

  _4bit u_4bit_1 (.D1(D1), .D2(D2), .C(C), .Q1(Q1), .Q2(Q2), .D3(D3), .Q3(Q3), .D4(D4), .Q4(Q4));
  _4bit u_4bit_2 (.D1(D5), .D2(D6), .C(C), .Q1(Q5), .Q2(Q6), .D3(D7), .Q3(Q7), .D4(D8), .Q4(Q8));
endmodule

module _16bit (
  input  D1,
  input  D2,
  input  D3,
  input  D4,
  input  D5,
  input  D6,
  input  D7,
  input  D8,
  input  D9,
  input  D10,
  input  D11,
  input  D12,
  input  D13,
  input  D14,
  input  D15,
  input  D16,
  input  C,
  output Q1,
  output Q2,
  output Q3,
  output Q4,
  output Q5,
  output Q6,
  output Q7,
  output Q8,
  output Q9,
  output Q10,
  output Q11,
  output Q12,
  output Q13,
  output Q14,
  output Q15,
  output Q16
);

  _8bit u_8bit_1 (
    .D1(D1), .D2(D2), .D3(D3), .D4(D4), .C(C), .Q1(Q1), .Q2(Q2), .Q3(Q3), .Q4(Q4), .D5(D5), .Q5(Q5), .D6(D6),
    .Q6(Q6), .D7(D7), .Q7(Q7), .D8(D8), .Q8(Q8));
  _8bit u_8bit_2 (
    .D1(D9), .D2(D10), .D3(D11), .D4(D12), .C(C), .Q1(Q9), .Q2(Q10), .Q3(Q11), .Q4(Q12), .D5(D13), .Q5(Q13),
    .D6(D14), .Q6(Q14), .D7(D15), .Q7(Q15), .D8(D16), .Q8(Q16));
endmodule

module _32bit (
  input  D1,
  input  D2,
  input  D3,
  input  D4,
  input  D5,
  input  D6,
  input  D7,
  input  D8,
  input  D9,
  input  D10,
  input  D11,
  input  D12,
  input  D13,
  input  D14,
  input  D15,
  input  D16,
  input  D17,
  input  D18,
  input  D19,
  input  D20,
  input  D21,
  input  D22,
  input  D23,
  input  D24,
  input  D25,
  input  D26,
  input  D27,
  input  D28,
  input  D29,
  input  D30,
  input  D31,
  input  D32,
  input  C,
  output Q1,
  output Q2,
  output Q3,
  output Q4,
  output Q5,
  output Q6,
  output Q7,
  output Q8,
  output Q9,
  output Q10,
  output Q11,
  output Q12,
  output Q13,
  output Q14,
  output Q15,
  output Q16,
  output Q17,
  output Q18,
  output Q19,
  output Q20,
  output Q21,
  output Q22,
  output Q23,
  output Q24,
  output Q25,
  output Q26,
  output Q27,
  output Q28,
  output Q29,
  output Q30,
  output Q31,
  output Q32
);

  _16bit u_16bit_1 (
    .D1(D1), .D2(D2), .D3(D3), .D4(D4), .D5(D5), .D6(D6), .D7(D7), .D8(D8), .D9(D9), .D11(D11), .D12(D12),
    .D13(D13), .D14(D14), .D15(D15), .D16(D16), .C(C), .Q1(Q1), .Q2(Q2), .Q3(Q3), .Q4(Q4), .Q5(Q5), .Q6(Q6),
    .Q7(Q7), .Q8(Q8), .Q9(Q9), .Q10(Q10), .Q11(Q11), .Q12(Q12), .Q13(Q13), .Q14(Q14), .Q15(Q15), .Q16(Q16),
    .D10(D10));
  _16bit u_16bit_2 (
    .D1(D17), .D2(D18), .D3(D19), .D4(D20), .D5(D21), .D6(D22), .D7(D23), .D8(D24), .D9(D25), .D11(D27),
    .D12(D28), .D13(D29), .D14(D30), .D15(D31), .D16(D32), .C(C), .Q1(Q17), .Q2(Q18), .Q3(Q19), .Q4(Q20),
    .Q5(Q21), .Q6(Q22), .Q7(Q23), .Q8(Q24), .Q9(Q25), .Q10(Q26), .Q11(Q27), .Q12(Q28), .Q13(Q29), .Q14(Q30),
    .Q15(Q31), .Q16(Q32), .D10(D26));
endmodule

module _64bit (
  input  D1,
  input  D2,
  input  D3,
  input  D4,
  input  D5,
  input  D6,
  input  D7,
  input  D8,
  input  D9,
  input  D10,
  input  D11,
  input  D12,
  input  D13,
  input  D14,
  input  D15,
  input  D16,
  input  D17,
  input  D18,
  input  D19,
  input  D20,
  input  D21,
  input  D22,
  input  D23,
  input  D24,
  input  D25,
  input  D26,
  input  D27,
  input  D28,
  input  D29,
  input  D30,
  input  D31,
  input  D32,
  input  D1_2,
  input  D2_2,
  input  D3_2,
  input  D4_2,
  input  D5_2,
  input  D6_2,
  input  D7_2,
  input  D8_2,
  input  D9_2,
  input  D10_2,
  input  D11_2,
  input  D12_2,
  input  D13_2,
  input  D14_2,
  input  D15_2,
  input  D16_2,
  input  D17_2,
  input  D18_2,
  input  D19_2,
  input  D20_2,
  input  D21_2,
  input  D22_2,
  input  D23_2,
  input  D24_2,
  input  D25_2,
  input  D26_2,
  input  D27_2,
  input  D28_2,
  input  D29_2,
  input  D30_2,
  input  D31_2,
  input  D32_2,
  input  \С ,
  output D1_3,
  output D2_3,
  output D3_3,
  output D4_3,
  output D5_3,
  output D6_3,
  output D7_3,
  output D8_3,
  output D9_3,
  output D10_3,
  output D11_3,
  output D12_3,
  output D13_3,
  output D14_3,
  output D15_3,
  output D16_3,
  output D17_3,
  output D18_3,
  output D19_3,
  output D20_3,
  output D21_3,
  output D22_3,
  output D23_3,
  output D24_3,
  output D25_3,
  output D26_3,
  output D27_3,
  output D28_3,
  output D29_3,
  output D30_3,
  output D31_3,
  output D32_3,
  output D31_4,
  output D32_4,
  output D33,
  output D4_4,
  output D5_4,
  output D6_4,
  output D7_4,
  output D8_4,
  output D9_4,
  output D10_4,
  output D11_4,
  output D12_4,
  output D13_4,
  output D14_4,
  output D15_4,
  output D16_4,
  output D17_4,
  output D18_4,
  output D19_4,
  output D20_4,
  output D21_4,
  output D22_4,
  output D23_4,
  output D24_4,
  output D25_4,
  output D26_4,
  output D27_4,
  output D28_4,
  output D29_4,
  output D30_4,
  output D31_5,
  output D32_5
);

  _32bit u_32bit_1 (
    .D1(D1), .Q1(D1_3), .D2(D2), .Q2(D2_3), .D3(D3), .Q3(D3_3), .D4(D4), .Q4(D4_3), .D5(D5), .Q5(D5_3),
    .D6(D6), .Q6(D6_3), .D7(D7), .Q7(D7_3), .D8(D8), .Q8(D8_3), .D9(D9), .D10(D10), .D11(D11), .D12(D12),
    .D13(D13), .D14(D14), .D15(D15), .D16(D16), .Q9(D9_3), .Q10(D10_3), .Q11(D11_3), .Q12(D12_3),
    .Q13(D13_3), .Q14(D14_3), .Q15(D15_3), .Q16(D16_3), .D17(D17), .Q17(D17_3), .D18(D18), .Q18(D18_3),
    .D19(D19), .Q19(D19_3), .D20(D20), .Q20(D20_3), .D21(D21), .Q21(D21_3), .D22(D22), .Q22(D22_3),
    .D23(D23), .Q23(D23_3), .D24(D24), .Q24(D24_3), .D25(D25), .Q25(D25_3), .D26(D26), .Q26(D26_3),
    .D27(D27), .Q27(D27_3), .D28(D28), .Q28(D28_3), .D29(D29), .Q29(D29_3), .D30(D30), .Q30(D30_3),
    .D31(D31), .Q31(D31_3), .D32(D32), .Q32(D32_3), .C(\С ));
  _32bit u_32bit_2 (
    .D1(D1_2), .Q1(D31_4), .D2(D2_2), .Q2(D32_4), .D3(D3_2), .Q3(D33), .D4(D4_2), .Q4(D4_4), .D5(D5_2),
    .Q5(D5_4), .D6(D6_2), .Q6(D6_4), .D7(D7_2), .Q7(D7_4), .D8(D8_2), .Q8(D8_4), .D9(D9_2), .D10(D10_2),
    .D11(D11_2), .D12(D12_2), .D13(D13_2), .D14(D14_2), .D15(D15_2), .D16(D16_2), .Q9(D9_4), .Q10(D10_4),
    .Q11(D11_4), .Q12(D12_4), .Q13(D13_4), .Q14(D14_4), .Q15(D15_4), .Q16(D16_4), .D17(D17_2), .Q17(D17_4),
    .D18(D18_2), .Q18(D18_4), .D19(D19_2), .Q19(D19_4), .D20(D20_2), .Q20(D20_4), .D21(D21_2), .Q21(D21_4),
    .D22(D22_2), .Q22(D22_4), .D23(D23_2), .Q23(D23_4), .D24(D24_2), .Q24(D24_4), .D25(D25_2), .Q25(D25_4),
    .D26(D26_2), .Q26(D26_4), .D27(D27_2), .Q27(D27_4), .D28(D28_2), .Q28(D28_4), .D29(D29_2), .Q29(D29_4),
    .D30(D30_2), .Q30(D30_4), .D31(D31_2), .Q31(D31_5), .D32(D32_2), .Q32(D32_5), .C(\С ));
endmodule

// 32768
module Main (
);

  wire C_out, x0_out, x1_out, x2_out, x3_out, x4_out, x5_out, x6_out, x7_out, x8_out, x9_out, x10_out,
       x11_out, x12_out, x13_out, x14_out, x15_out, x16_out, x17_out, x18_out, x19_out, x20_out, x21_out,
       x22_out, x23_out, x24_out, x25_out, x26_out, x27_out, x28_out, x29_out, x30_out, x31_out, x32_out,
       x33_out, x34_out, x35_out, x36_out, x37_out, x38_out, x39_out, x40_out, x41_out, x42_out, x43_out,
       x44_out, x45_out, x46_out, x47_out, x48_out, x49_out, x50_out, x51_out, x52_out, x53_out, x54_out,
       x55_out, x56_out, x57_out, x58_out, x59_out, x60_out, x61_out, x62_out, x63_out;
  wire [3:0] n64bit_1_d1_3, n64bit_1_d5_3, n64bit_1_d5_4, n64bit_1_d9_3, n64bit_1_d9_4, n64bit_1_d13_3,
       n64bit_1_d13_4, n64bit_1_d17_3, n64bit_1_d17_4, n64bit_1_d21_3, n64bit_1_d21_4, n64bit_1_d25_3,
       n64bit_1_d25_4, n64bit_1_d29_3, n64bit_1_d29_4, n64bit_1_d31_4;

  Clock x0 (.out(x0_out));
  Clock #(.highDuration(2), .lowDuration(2)) x1 (.out(x1_out));
  Clock #(.highDuration(4), .lowDuration(4)) x2 (.out(x2_out));
  Clock #(.highDuration(8), .lowDuration(8)) x3 (.out(x3_out));
  Clock #(.highDuration(16), .lowDuration(16)) x4 (.out(x4_out));
  Clock #(.highDuration(32), .lowDuration(32)) x5 (.out(x5_out));
  Clock #(.highDuration(64), .lowDuration(64)) x6 (.out(x6_out));
  Clock #(.highDuration(128), .lowDuration(128)) x7 (.out(x7_out));
  Clock #(.highDuration(256), .lowDuration(256)) x8 (.out(x8_out));
  Clock #(.highDuration(512), .lowDuration(512)) x9 (.out(x9_out));
  Clock #(.highDuration(1024), .lowDuration(1024)) x10 (.out(x10_out));
  Clock #(.highDuration(2048), .lowDuration(2048)) x11 (.out(x11_out));
  Clock #(.highDuration(4096), .lowDuration(4096)) x12 (.out(x12_out));
  Clock #(.highDuration(8192), .lowDuration(8192)) x13 (.out(x13_out));
  Clock #(.highDuration(16384), .lowDuration(16384)) x14 (.out(x14_out));
  Clock #(.highDuration(32768), .lowDuration(32768)) x15 (.out(x15_out));
  Clock #(.highDuration(65536), .lowDuration(65536)) x16 (.out(x16_out));
  Clock #(.highDuration(131072), .lowDuration(131072)) x17 (.out(x17_out));
  Clock #(.highDuration(262144), .lowDuration(262144)) x18 (.out(x18_out));
  Clock #(.highDuration(524288), .lowDuration(524288)) x19 (.out(x19_out));
  Clock #(.highDuration(1048576), .lowDuration(1048576)) x20 (.out(x20_out));
  Clock #(.highDuration(2097152), .lowDuration(2097152)) x21 (.out(x21_out));
  Clock #(.highDuration(4194304), .lowDuration(4194304)) x22 (.out(x22_out));
  Clock #(.highDuration(8388608), .lowDuration(8388608)) x23 (.out(x23_out));
  Clock #(.highDuration(16777216), .lowDuration(16777216)) x24 (.out(x24_out));
  Clock #(.highDuration(33554432), .lowDuration(33554432)) x25 (.out(x25_out));
  Clock #(.highDuration(6710886), .lowDuration(6710886)) x26 (.out(x26_out));
  Clock #(.highDuration(134217728), .lowDuration(134217728)) x27 (.out(x27_out));
  Clock #(.highDuration(268435456), .lowDuration(268435456)) x28 (.out(x28_out));
  Clock #(.highDuration(536870912), .lowDuration(536870912)) x29 (.out(x29_out));
  Clock #(.highDuration(1073741824), .lowDuration(1073741824)) x30 (.out(x30_out));
  Clock x31 (.out(x31_out));
  Clock #(.highDuration(2), .lowDuration(2)) x32 (.out(x32_out));
  Clock #(.highDuration(4), .lowDuration(4)) x33 (.out(x33_out));
  Clock #(.highDuration(8), .lowDuration(8)) x34 (.out(x34_out));
  Clock #(.highDuration(16), .lowDuration(16)) x35 (.out(x35_out));
  Clock #(.highDuration(32), .lowDuration(32)) x36 (.out(x36_out));
  Clock #(.highDuration(64), .lowDuration(64)) x37 (.out(x37_out));
  Clock #(.highDuration(128), .lowDuration(128)) x38 (.out(x38_out));
  Clock #(.highDuration(256), .lowDuration(256)) x39 (.out(x39_out));
  Clock #(.highDuration(512), .lowDuration(512)) x40 (.out(x40_out));
  Clock #(.highDuration(1024), .lowDuration(1024)) x41 (.out(x41_out));
  Clock #(.highDuration(2048), .lowDuration(2048)) x42 (.out(x42_out));
  Clock #(.highDuration(4096), .lowDuration(4096)) x43 (.out(x43_out));
  Clock #(.highDuration(8192), .lowDuration(8192)) x44 (.out(x44_out));
  Clock #(.highDuration(16384), .lowDuration(16384)) x45 (.out(x45_out));
  Clock #(.highDuration(32768), .lowDuration(32768)) x46 (.out(x46_out));
  Clock #(.highDuration(65536), .lowDuration(65536)) x47 (.out(x47_out));
  Clock #(.highDuration(131072), .lowDuration(131072)) x48 (.out(x48_out));
  Clock #(.highDuration(262144), .lowDuration(262144)) x49 (.out(x49_out));
  Clock #(.highDuration(524288), .lowDuration(524288)) x50 (.out(x50_out));
  Clock #(.highDuration(1048576), .lowDuration(1048576)) x51 (.out(x51_out));
  Clock #(.highDuration(2097152), .lowDuration(2097152)) x52 (.out(x52_out));
  Clock #(.highDuration(4194304), .lowDuration(4194304)) x53 (.out(x53_out));
  Clock #(.highDuration(8388608), .lowDuration(8388608)) x54 (.out(x54_out));
  Clock #(.highDuration(16777216), .lowDuration(16777216)) x55 (.out(x55_out));
  Clock #(.highDuration(33554432), .lowDuration(33554432)) x56 (.out(x56_out));
  Clock #(.highDuration(6710886), .lowDuration(6710886)) x57 (.out(x57_out));
  Clock #(.highDuration(134217728), .lowDuration(134217728)) x58 (.out(x58_out));
  Clock #(.highDuration(268435456), .lowDuration(268435456)) x59 (.out(x59_out));
  Clock #(.highDuration(536870912), .lowDuration(536870912)) x60 (.out(x60_out));
  Clock #(.highDuration(1073741824), .lowDuration(1073741824)) x61 (.out(x61_out));
  Clock x62 (.out(x62_out));
  Clock #(.highDuration(2), .lowDuration(2)) x63 (.out(x63_out));
  Clock #(.highDuration(2), .lowDuration(3)) C (.out(C_out));
  _64bit u_64bit_1 (
    .D1(x0_out), .D2(x1_out), .D3(x2_out), .D4(x3_out), .D5(x4_out), .D6(x5_out), .D7(x6_out), .D8(x7_out),
    .D9(x8_out), .D10(x9_out), .D11(x10_out), .D12(x11_out), .D13(x12_out), .D14(x13_out), .D15(x14_out),
    .D16(x15_out), .D17(x16_out), .D18(x17_out), .D19(x18_out), .D20(x19_out), .D21(x20_out), .D22(x21_out),
    .D23(x22_out), .D24(x23_out), .D25(x24_out), .D26(x25_out), .D27(x26_out), .D28(x27_out), .D29(x28_out),
    .D30(x29_out), .D31(x30_out), .D32(x31_out), .D1_2(x32_out), .D2_2(x33_out), .D3_2(x34_out),
    .D4_2(x35_out), .D5_2(x36_out), .D6_2(x37_out), .D7_2(x38_out), .D8_2(x39_out), .D9_2(x40_out),
    .D10_2(x41_out), .D11_2(x42_out), .D12_2(x43_out), .D13_2(x44_out), .D14_2(x45_out), .D15_2(x46_out),
    .D16_2(x47_out), .D17_2(x48_out), .D18_2(x49_out), .D19_2(x50_out), .D20_2(x51_out), .D21_2(x52_out),
    .D22_2(x53_out), .D23_2(x54_out), .D24_2(x55_out), .D25_2(x56_out), .D26_2(x57_out), .D27_2(x58_out),
    .D28_2(x59_out), .D29_2(x60_out), .D30_2(x61_out), .D31_2(x62_out), .D32_2(x63_out), .\С (C_out),
    .D1_3(n64bit_1_d1_3[0]), .D2_3(n64bit_1_d1_3[1]), .D3_3(n64bit_1_d1_3[2]), .D4_3(n64bit_1_d1_3[3]),
    .D5_3(n64bit_1_d5_3[0]), .D6_3(n64bit_1_d5_3[1]), .D7_3(n64bit_1_d5_3[2]), .D8_3(n64bit_1_d5_3[3]),
    .D9_3(n64bit_1_d9_3[0]), .D10_3(n64bit_1_d9_3[1]), .D11_3(n64bit_1_d9_3[2]), .D12_3(n64bit_1_d9_3[3]),
    .D13_3(n64bit_1_d13_3[0]), .D14_3(n64bit_1_d13_3[1]), .D15_3(n64bit_1_d13_3[2]),
    .D16_3(n64bit_1_d13_3[3]), .D17_3(n64bit_1_d17_3[0]), .D18_3(n64bit_1_d17_3[1]),
    .D19_3(n64bit_1_d17_3[2]), .D20_3(n64bit_1_d17_3[3]), .D21_3(n64bit_1_d21_3[0]),
    .D22_3(n64bit_1_d21_3[1]), .D23_3(n64bit_1_d21_3[2]), .D24_3(n64bit_1_d21_3[3]),
    .D25_3(n64bit_1_d25_3[0]), .D26_3(n64bit_1_d25_3[1]), .D27_3(n64bit_1_d25_3[2]),
    .D28_3(n64bit_1_d25_3[3]), .D29_3(n64bit_1_d29_3[0]), .D30_3(n64bit_1_d29_3[1]),
    .D31_3(n64bit_1_d29_3[2]), .D32_3(n64bit_1_d29_3[3]), .D31_4(n64bit_1_d31_4[0]),
    .D32_4(n64bit_1_d31_4[1]), .D33(n64bit_1_d31_4[2]), .D4_4(n64bit_1_d31_4[3]), .D5_4(n64bit_1_d5_4[0]),
    .D6_4(n64bit_1_d5_4[1]), .D7_4(n64bit_1_d5_4[2]), .D8_4(n64bit_1_d5_4[3]), .D9_4(n64bit_1_d9_4[0]),
    .D10_4(n64bit_1_d9_4[1]), .D11_4(n64bit_1_d9_4[2]), .D12_4(n64bit_1_d9_4[3]), .D13_4(n64bit_1_d13_4[0]),
    .D14_4(n64bit_1_d13_4[1]), .D15_4(n64bit_1_d13_4[2]), .D17_4(n64bit_1_d17_4[0]),
    .D18_4(n64bit_1_d17_4[1]), .D19_4(n64bit_1_d17_4[2]), .D20_4(n64bit_1_d17_4[3]),
    .D21_4(n64bit_1_d21_4[0]), .D22_4(n64bit_1_d21_4[1]), .D23_4(n64bit_1_d21_4[2]),
    .D24_4(n64bit_1_d21_4[3]), .D25_4(n64bit_1_d25_4[0]), .D26_4(n64bit_1_d25_4[1]),
    .D27_4(n64bit_1_d25_4[2]), .D28_4(n64bit_1_d25_4[3]), .D29_4(n64bit_1_d29_4[0]),
    .D30_4(n64bit_1_d29_4[1]), .D31_5(n64bit_1_d29_4[2]), .D32_5(n64bit_1_d29_4[3]), .D16_4(n64bit_1_d13_4[3]));
  Hex_Digit_Display hex_digit_display_1 (.value(n64bit_1_d25_4));  // open: dp
  Hex_Digit_Display hex_digit_display_2 (.value(n64bit_1_d29_4));  // open: dp
  Hex_Digit_Display hex_digit_display_3 (.value(n64bit_1_d21_4));  // open: dp
  Hex_Digit_Display hex_digit_display_4 (.value(n64bit_1_d13_4));  // open: dp
  Hex_Digit_Display hex_digit_display_5 (.value(n64bit_1_d17_4));  // open: dp
  Hex_Digit_Display hex_digit_display_6 (.value(n64bit_1_d9_4));  // open: dp
  Hex_Digit_Display hex_digit_display_7 (.value(n64bit_1_d5_4));  // open: dp
  Hex_Digit_Display hex_digit_display_8 (.value(n64bit_1_d31_4));  // open: dp
  Hex_Digit_Display hex_digit_display_9 (.value(n64bit_1_d29_3));  // open: dp
  Hex_Digit_Display hex_digit_display_10 (.value(n64bit_1_d25_3));  // open: dp
  Hex_Digit_Display hex_digit_display_11 (.value(n64bit_1_d21_3));  // open: dp
  Hex_Digit_Display hex_digit_display_12 (.value(n64bit_1_d17_3));  // open: dp
  Hex_Digit_Display hex_digit_display_13 (.value(n64bit_1_d13_3));  // open: dp
  Hex_Digit_Display hex_digit_display_14 (.value(n64bit_1_d9_3));  // open: dp
  Hex_Digit_Display hex_digit_display_15 (.value(n64bit_1_d1_3));  // open: dp
  Hex_Digit_Display hex_digit_display_16 (.value(n64bit_1_d5_3));  // open: dp
endmodule
